# Fritzing sketch knockLock_upgraded (saved by Fritzing 0.9.3b)
breadboards: 1

parts:
  Composant1 = Arduino Uno (Rev3)
  R1 = Resistor [tolerance=±5% resistance=220 package=THT]
  LED1 = LED - 5mm [color="Red (633nm)" package="5 mm [THT]"]
  R2 = Resistor [tolerance=±5% resistance=220 package=THT]
  LED2 = LED - 5mm [color="Green (560nm)" package="5 mm [THT]"]
  J1 = Piezo Speaker
  R4 = Resistor [tolerance=±5% resistance=1M package=THT]
  S1 = Pushbutton [package="[THT]"]
  R5 = Resistor [tolerance=±5% resistance=10k package=THT]
  C1 = Electrolytic Capacitor [capacitance=0.1mF package="100 mil [THT, electrolytic]"]
  J2 = Basic Servo
  S2 = Pushbutton [package="[THT]"]  # not connected

nets:
  N1: Composant1.A0, J1.pin1, R4.Pin_1
  N2: Composant1.D9_PWM, J2.pulse
  N3: Composant1.D2, S1.Pin_1, S1.Pin_2
  N4: Composant1.D4, R2.Pin_0
  N5: Composant1.D5_PWM, R1.Pin_0
  5V: Composant1.5V, J1.pin2, S1.Pin_3, S1.Pin_4, C1.-, J2.vcc
  GND: Composant1.GND, LED1.cathode, LED2.cathode, R4.Pin_0, R5.Pin_0, C1.+, J2.gnd
  N6: R1.Pin_1, LED1.anode
  N7: R2.Pin_1, LED2.anode
